// Digital circuit controlUnit.dig as structural Verilog
// generates control signals for datapath
module controlUnit (
  input  clock,
  input  reset,
  input  [15:0] dIn,
  input  alt,
  input  NE,
  input  GE,
  output wr,
  output rd,
  output sign,
  output word,
  output sub,
  output \logic ,
  output [1:0] logSelect,
  output [11:0] topImm,
  output even,
  output const2,
  output selImm,
  output selConst,
  output Azero,
  output we,
  output [3:0] Rw,
  output [3:0] Ra,
  output [3:0] Rb,
  output selRd,
  output slt,
  output immLow
);

  wire and_1_out, and_2_out, and_3_out, and_5_out, and_6_out, and_7_out, and_8_out, and_9_out, and_10_out,
       and_11_out, and_18_out, and_19_out, branch, cond, E, EJ, F, FJorBT, imm, IR2, IR3, multiplexer_1_out,
       or_2_out, or_8_out, prefix_q, xor_1_out, zD, zS1, zS2;
  wire [11:0] multiplexer_2_out;
  wire [15:8] IR_q;

  Multiplexer multiplexer_1 (.sel(logSelect[0]), .in_0(NE), .in_1(GE), .out(multiplexer_1_out));
  xor xor_1 (xor_1_out, multiplexer_1_out, alt);
  Multiplexer #(.Bits(12)) multiplexer_2 (.sel(E), .in_0({IR_q, Rb}), .in_1({12{1'b0}}), .out(multiplexer_2_out));
  and and_1 (and_1_out, ~dIn[0], ~dIn[1], ~dIn[2], ~dIn[3], F);  // And
  and and_2 (and_2_out, ~IR3, ~IR2, ~logSelect[1], ~logSelect[0]);  // And
  Register #(.Bits(16)) IR (.D(dIn), .C(clock), .en(F), .Q({IR_q, Rb, IR3, IR2, logSelect}));
  D_FF #(.Bits(12)) IM (.D(multiplexer_2_out), .C(clock), .Q(topImm));  // open: nQ
  D_FF fetch (.D(or_2_out), .C(clock), .Q(F), .nQ(E));
  or or_1 (imm, prefix_q, ~IR3);  // Or
  or or_2 (or_2_out, E, reset, and_1_out);
  D_FF d_ff_1 (.D(xor_1_out), .C(clock), .Q(cond));  // open: nQ
  Register prefix (.D(and_2_out), .C(clock), .en(F), .Q(prefix_q));
  and and_3 (and_3_out, ~IR3, ~IR2, ~logSelect[1], logSelect[0]);  // And
  and and_4 (zS2, ~Rb[0], ~Rb[1], ~Rb[2], ~Rb[3]);  // And
  and and_5 (and_5_out, E, ~IR2, ~logSelect[1], ~logSelect[0]);  // And
  and and_6 (and_6_out, E, ~IR3, IR2);  // And
  and and_7 (and_7_out, and_3_out, alt);
  or or_3 (selRd, and_5_out, and_6_out);
  and and_8 (and_8_out, F, ~and_7_out);  // And
  and and_9 (and_9_out, F, ~reset);  // And
  and and_10 (and_10_out, ~EJ, E, imm);  // And
  and and_11 (and_11_out, F, ~FJorBT);  // And
  r0 r0_1 (.rin(IR_q[11:8]), .pc(or_8_out), .rout(Ra), .z(zS1));
  and and_12 (wr, E, ~IR3, IR2, logSelect[1]);  // And
  or or_4 (rd, F, ~logSelect[1]);  // Or
  and and_13 (sub, E, ~IR2, logSelect[1]);  // And
  and and_14 (\logic , E, IR3, IR2);
  nand nand_1 (we, E, branch);
  r0 r0_2 (.rin(IR_q[15:12]), .pc(F), .rout(Rw), .z(zD));
  and and_15 (slt, E, ~IR2, logSelect[1], logSelect[0]);  // And
  and and_16 (branch, ~IR3, ~IR2, logSelect[1]);  // And
  and and_17 (EJ, E, and_3_out);
  and and_18 (and_18_out, F, and_3_out);
  and and_19 (and_19_out, F, branch, cond);
  or or_5 (const2, and_9_out, EJ);
  or or_6 (selImm, FJorBT, and_10_out);
  or or_7 (selConst, EJ, and_11_out);
  and and_20 (immLow, F, branch);
  or or_8 (or_8_out, and_8_out, EJ);
  or or_9 (FJorBT, and_18_out, and_19_out);
  not not_1 (sign, IR3);

  assign Azero = reset;
  assign even = const2;
  assign word = logSelect[0];

  // Other names for the same wires on the sheet: IR0 = logSelect[0]; IR1 = logSelect[1]

  // Notes on the sheet:
  //   clock: controls internal registers
  //   reset: when high forces the PC to 0x0000
  //   dIn: data from memory
  //   alt: immediate value indicates alternative instruction in lowest bit
  //   NE: A ~= B
  //   GE: A >= B
  //   wr: memory write cycle
  //   rd: memory read cycle
  //   sign: not LBU
  //   word: not SB, LB or LBU
  //   sub: change addition to subtraction
  //   logic: select logic operation instead of addition
  //   logSelect: selects between shift right, AND, OR, XOR
  //   topImm: saved from prefix instruction
  //   even: forces bottom bit of immediate to 0
  //   const2: changes constant from 0 to 2
  //   selImm: B is immediate
  //   selConst: B is a constant
  //   Azero: force A to 0
  //   we: updates register Rw
  //   Rw: register to be written
  //   Ra: first register to read
  //   Rb: second register to read
  //   selRd: selects betweenALU result and memory for write back
  //   slt: ignores ALU result and use GE?0x0000:0x0001
  //   immLow: selects either field rS2 or rD for the 4 lower bits of immediate
endmodule
