// Digital circuit drv16.dig as structural Verilog
// 16 bit processor which is compatible at the assembly language level with RISC-V
module drv16 (
  input  clock,
  input  reset,
  input  [15:0] dIn,
  output [14:0] addr,
  output wr,
  output [15:0] dOut,
  output rd
);

  wire adapt_1_p5, adapt_1_p6, adapt_1_p7, undriven;
  wire [0:0] multiplexer_2_out;
  wire [3:0] adapt_1_p3, adapt_1_p4;
  wire [15:0] alu_1_p3, bytes_1_tord, multiplexer_1_out, registerfile_1_da, registerfile_1_db;

  Multiplexer #(.Bits(16)) multiplexer_1 (
    .sel(undriven), .in_0(alu_1_p3), .in_1(bytes_1_tord), .out(multiplexer_1_out));
  RegisterFile #(.AddrBits(4), .Bits(16)) registerfile_1 (
    .Din(multiplexer_1_out), .Rw(adapt_1_p3), .C(clock), .Rb(adapt_1_p4), .Da(registerfile_1_da),
    .Db(registerfile_1_db));  // open: we, Ra
  // adapt adapt_1: pin names not known; wires that end beside it: registerfile_1_da, registerfile_1_db, adapt_1_p3, adapt_1_p4, adapt_1_p5, adapt_1_p6, adapt_1_p7
  bytes bytes_1 (
    .dIn(dIn), .A0(multiplexer_2_out[0]), .fromRS2(registerfile_1_db), .dOut(dOut), .toRD(bytes_1_tord));  // open: sign, word
  // alu alu_1: pin names not known; wires that end beside it: adapt_1_p5, adapt_1_p6, alu_1_p3, wr
  Multiplexer #(.Bits(16)) multiplexer_2 (
    .sel(adapt_1_p7), .in_0(alu_1_p3), .in_1(registerfile_1_da), .out({addr, multiplexer_2_out[0]}));

  // Notes on the sheet:
  //   addr: selects a 16 bit word in memory to be read or changed
  //   wr: indicates a write operation
  //   dOut: word to be sent to memory
  //   reset: when high prepares the processor to execute from address 0
  //   dIn: word coming from memory
  //   rd: indicates that memory will be read in this cycle
endmodule
