// Digital circuit system.dig as structural Verilog
module system (
  input  clk
);

  wire and_1_out, comparator_1_eq, drv16_1_wr, reset_out;
  wire [14:0] drv16_1_addr;
  wire [15:0] drv16_1_dout, ramdualport_1_d;

  Button reset (.out(reset_out));
  drv16 drv16_1 (
    .clock(clk), .reset(reset_out), .dIn(ramdualport_1_d), .addr(drv16_1_addr), .wr(drv16_1_wr),
    .dOut(drv16_1_dout));  // open: rd
  Comparator #(.Bits(15)) comparator_1 (.a({15{1'b1}}), .b(drv16_1_addr), .eq(comparator_1_eq));  // open: gt, lt
  RAMDualPort #(.AddrBits(15), .isProgramMemory("true"), .Bits(16)) ramdualport_1 (
    .A(drv16_1_addr), .Din(drv16_1_dout), .str(drv16_1_wr), .C(clk), .ld(1'b1), .D(ramdualport_1_d));
  and and_1 (and_1_out, comparator_1_eq, drv16_1_wr);
  Terminal terminal_1 (.D(drv16_1_dout), .C(clk), .en(and_1_out));
endmodule
